// Logisim project AlarmaEncendida.circ as structural Verilog: 4 circuits, main circuit main
module main (
);

  wire alarmaencendida_1_out_33, and_1_out, and_2_out, and_3_out, and_4_out, and_5_out, and_6_out,
       button_1_out, button_2_out, clock_1_out, cont4bit_1_q0, cont4bit_1_q1, cont4bit_1_q2, cont4bit_1_q3,
       cont4bit_2_q0, cont4bit_2_q1, cont4bit_2_q2, cont4bit_2_q3, cont4bit_3_q0, cont4bit_3_q1,
       cont4bit_3_q2, cont4bit_3_q3, cont4bit_4_q0, cont4bit_4_q1, cont4bit_4_q2, cont4bit_4_q3,
       cont4bit_5_q0, cont4bit_5_q1, cont4bit_5_q2, cont4bit_5_q3, cont4bit_6_q0, cont4bit_6_q1,
       cont4bit_6_q2, cont4bit_6_q3, decoled_1_o1, decoled_1_o2, decoled_1_o3, decoled_1_o5, decoled_1_o6,
       decoled_1_o7, decoled_1_o8, decoled_2_o1, decoled_2_o2, decoled_2_o3, decoled_2_o5, decoled_2_o6,
       decoled_2_o7, decoled_2_o8, decoled_3_o1, decoled_3_o2, decoled_3_o3, decoled_3_o5, decoled_3_o6,
       decoled_3_o7, decoled_3_o8, decoled_4_o1, decoled_4_o2, decoled_4_o3, decoled_4_o5, decoled_4_o6,
       decoled_4_o7, decoled_4_o8, decoled_5_o1, decoled_5_o2, decoled_5_o3, decoled_5_o5, decoled_5_o6,
       decoled_5_o7, decoled_5_o8, decoled_6_o1, decoled_6_o2, decoled_6_o3, decoled_6_o5, decoled_6_o6,
       decoled_6_o7, decoled_6_o8, or_1_out, or_2_out, or_3_out;

  Button button_1 (.out(button_1_out));
  Button button_2 (.out(button_2_out));
  Button button_3 ();  // open: out
  LED led_1 ();  // open: in
  LED led_2 ();  // open: in
  and and_1 (and_1_out, cont4bit_2_q2, cont4bit_1_q1);
  _7_Segment_Display u_7_segment_display_1 (
    .g(decoled_1_o5), .f(decoled_1_o6), .a(decoled_1_o7), .b(decoled_1_o8), .e(decoled_1_o1),
    .d(decoled_1_o2), .c(decoled_1_o3));  // open: dp
  DecoLED decoled_1 (
    .I4(cont4bit_1_q3), .I3(cont4bit_1_q2), .I2(cont4bit_1_q1), .I1(cont4bit_1_q0), .o1(decoled_1_o1),
    .o2(decoled_1_o2), .o3(decoled_1_o3), .o5(decoled_1_o5), .o6(decoled_1_o6), .o7(decoled_1_o7),
    .o8(decoled_1_o8));
  Cont4Bit cont4bit_1 (
    .T(and_2_out), .Reset(and_1_out), .Q3(cont4bit_1_q3), .Q2(cont4bit_1_q2), .Q1(cont4bit_1_q1),
    .Q0(cont4bit_1_q0));
  _7_Segment_Display u_7_segment_display_2 (
    .g(decoled_2_o5), .f(decoled_2_o6), .a(decoled_2_o7), .b(decoled_2_o8), .e(decoled_2_o1),
    .d(decoled_2_o2), .c(decoled_2_o3));  // open: dp
  DecoLED decoled_2 (
    .I4(cont4bit_2_q3), .I3(cont4bit_2_q2), .I2(cont4bit_2_q1), .I1(cont4bit_2_q0), .o1(decoled_2_o1),
    .o2(decoled_2_o2), .o3(decoled_2_o3), .o5(decoled_2_o5), .o6(decoled_2_o6), .o7(decoled_2_o7),
    .o8(decoled_2_o8));
  Cont4Bit cont4bit_2 (
    .T(or_2_out), .Reset(or_1_out), .Q3(cont4bit_2_q3), .Q2(cont4bit_2_q2), .Q1(cont4bit_2_q1),
    .Q0(cont4bit_2_q0));
  and and_2 (and_2_out, cont4bit_2_q3, cont4bit_2_q1);
  or or_1 (or_1_out, and_2_out, and_1_out);
  LED led_3 (.in(clock_1_out));
  LED led_4 (.in(clock_1_out));
  and and_3 (and_3_out, cont4bit_3_q2, cont4bit_3_q1);
  or or_2 (or_2_out, and_3_out, button_1_out);
  LED led_5 (.in(alarmaencendida_1_out_33));
  AlarmaEncendida alarmaencendida_1 (.out_33(alarmaencendida_1_out_33));  // open: A, a_2, B, b_2, C, c_2, D, d_2, E, e_2, F, f_2, G, g_2, H, h_2, I, i_2, J, j_2, K, k_2, L, l_2, M, m_2, N, n_2, O, o_2, P, p_2
  _7_Segment_Display u_7_segment_display_3 (
    .g(decoled_3_o5), .f(decoled_3_o6), .a(decoled_3_o7), .b(decoled_3_o8), .e(decoled_3_o1),
    .d(decoled_3_o2), .c(decoled_3_o3));  // open: dp
  DecoLED decoled_3 (
    .I4(cont4bit_3_q3), .I3(cont4bit_3_q2), .I2(cont4bit_3_q1), .I1(cont4bit_3_q0), .o1(decoled_3_o1),
    .o2(decoled_3_o2), .o3(decoled_3_o3), .o5(decoled_3_o5), .o6(decoled_3_o6), .o7(decoled_3_o7),
    .o8(decoled_3_o8));
  Cont4Bit cont4bit_3 (
    .T(and_4_out), .Reset(and_3_out), .Q3(cont4bit_3_q3), .Q2(cont4bit_3_q2), .Q1(cont4bit_3_q1),
    .Q0(cont4bit_3_q0));
  _7_Segment_Display u_7_segment_display_4 (
    .g(decoled_4_o5), .f(decoled_4_o6), .a(decoled_4_o7), .b(decoled_4_o8), .e(decoled_4_o1),
    .d(decoled_4_o2), .c(decoled_4_o3));  // open: dp
  DecoLED decoled_4 (
    .I4(cont4bit_4_q3), .I3(cont4bit_4_q2), .I2(cont4bit_4_q1), .I1(cont4bit_4_q0), .o1(decoled_4_o1),
    .o2(decoled_4_o2), .o3(decoled_4_o3), .o5(decoled_4_o5), .o6(decoled_4_o6), .o7(decoled_4_o7),
    .o8(decoled_4_o8));
  and and_4 (and_4_out, cont4bit_4_q3, cont4bit_4_q1);
  LED led_6 (.in(clock_1_out));
  LED led_7 (.in(clock_1_out));
  Cont4Bit cont4bit_4 (
    .T(or_3_out), .Reset(and_4_out), .Q3(cont4bit_4_q3), .Q2(cont4bit_4_q2), .Q1(cont4bit_4_q1),
    .Q0(cont4bit_4_q0));
  or or_3 (or_3_out, and_5_out, button_2_out);
  _7_Segment_Display u_7_segment_display_5 (
    .g(decoled_5_o5), .f(decoled_5_o6), .a(decoled_5_o7), .b(decoled_5_o8), .e(decoled_5_o1),
    .d(decoled_5_o2), .c(decoled_5_o3));  // open: dp
  DecoLED decoled_5 (
    .I4(cont4bit_5_q3), .I3(cont4bit_5_q2), .I2(cont4bit_5_q1), .I1(cont4bit_5_q0), .o1(decoled_5_o1),
    .o2(decoled_5_o2), .o3(decoled_5_o3), .o5(decoled_5_o5), .o6(decoled_5_o6), .o7(decoled_5_o7),
    .o8(decoled_5_o8));
  Cont4Bit cont4bit_5 (
    .T(and_6_out), .Reset(and_5_out), .Q3(cont4bit_5_q3), .Q2(cont4bit_5_q2), .Q1(cont4bit_5_q1),
    .Q0(cont4bit_5_q0));
  and and_5 (and_5_out, cont4bit_5_q2, cont4bit_5_q1);
  and and_6 (and_6_out, cont4bit_6_q3, cont4bit_6_q1);
  _7_Segment_Display u_7_segment_display_6 (
    .g(decoled_6_o5), .f(decoled_6_o6), .a(decoled_6_o7), .b(decoled_6_o8), .e(decoled_6_o1),
    .d(decoled_6_o2), .c(decoled_6_o3));  // open: dp
  DecoLED decoled_6 (
    .I4(cont4bit_6_q3), .I3(cont4bit_6_q2), .I2(cont4bit_6_q1), .I1(cont4bit_6_q0), .o1(decoled_6_o1),
    .o2(decoled_6_o2), .o3(decoled_6_o3), .o5(decoled_6_o5), .o6(decoled_6_o6), .o7(decoled_6_o7),
    .o8(decoled_6_o8));
  Cont4Bit cont4bit_6 (
    .T(clock_1_out), .Reset(and_6_out), .Q3(cont4bit_6_q3), .Q2(cont4bit_6_q2), .Q1(cont4bit_6_q1),
    .Q0(cont4bit_6_q0));
  Clock clock_1 (.out(clock_1_out));

  // Notes on the sheet:
  //   Botones
  //   Ajuste
  //   Hora Actual
  //   Hora
  //   Alarma Sonando
  //   Minutos
  //   Segundos
endmodule

module AlarmaEncendida (
  input  A,
  input  a_2,
  input  B,
  input  b_2,
  input  C,
  input  c_2,
  input  D,
  input  d_2,
  input  E,
  input  e_2,
  input  F,
  input  f_2,
  input  G,
  input  g_2,
  input  H,
  input  h_2,
  input  I,
  input  i_2,
  input  J,
  input  j_2,
  input  K,
  input  k_2,
  input  L,
  input  l_2,
  input  M,
  input  m_2,
  input  N,
  input  n_2,
  input  O,
  input  o_2,
  input  P,
  input  p_2,
  output out_33
);

  wire comparator_1_eq, comparator_2_eq, comparator_3_eq, comparator_4_eq, comparator_5_eq, comparator_6_eq,
       comparator_7_eq, comparator_8_eq, comparator_9_eq, comparator_11_eq, comparator_13_eq,
       comparator_14_eq, comparator_15_eq, comparator_16_eq;

  Comparator #(.width(1)) comparator_1 (.a(A), .b(a_2), .eq(comparator_1_eq));  // open: gt, lt
  Comparator #(.width(1)) comparator_2 (.a(B), .b(b_2), .eq(comparator_2_eq));  // open: gt, lt
  Comparator #(.width(1)) comparator_3 (.a(C), .b(c_2), .eq(comparator_3_eq));  // open: gt, lt
  Comparator #(.width(1)) comparator_4 (.a(D), .b(d_2), .eq(comparator_4_eq));  // open: gt, lt
  Comparator #(.width(1)) comparator_5 (.a(E), .b(e_2), .eq(comparator_5_eq));  // open: gt, lt
  Comparator #(.width(1)) comparator_6 (.a(F), .b(f_2), .eq(comparator_6_eq));  // open: gt, lt
  Comparator #(.width(1)) comparator_7 (.a(G), .b(g_2), .eq(comparator_7_eq));  // open: gt, lt
  Comparator #(.width(1)) comparator_8 (.a(H), .b(h_2), .eq(comparator_8_eq));  // open: gt, lt
  Comparator #(.width(1)) comparator_9 (.a(I), .b(i_2), .eq(comparator_9_eq));  // open: gt, lt
  Comparator #(.width(1)) comparator_10 (.a(J), .b(j_2), .eq(comparator_9_eq));  // open: gt, lt
  Comparator #(.width(1)) comparator_11 (.a(K), .b(k_2), .eq(comparator_11_eq));  // open: gt, lt
  Comparator #(.width(1)) comparator_12 (.a(L), .b(l_2), .eq(comparator_11_eq));  // open: gt, lt
  Comparator #(.width(1)) comparator_13 (.a(M), .b(m_2), .eq(comparator_13_eq));  // open: gt, lt
  Comparator #(.width(1)) comparator_14 (.a(N), .b(n_2), .eq(comparator_14_eq));  // open: gt, lt
  Comparator #(.width(1)) comparator_15 (.a(O), .b(o_2), .eq(comparator_15_eq));  // open: gt, lt
  Comparator #(.width(1)) comparator_16 (.a(P), .b(p_2), .eq(comparator_16_eq));  // open: gt, lt
  and and_1 (out_33, comparator_1_eq, comparator_2_eq, comparator_3_eq, comparator_4_eq, comparator_5_eq, comparator_6_eq, comparator_7_eq, comparator_8_eq, comparator_9_eq, comparator_9_eq, comparator_11_eq, comparator_11_eq, comparator_13_eq, comparator_14_eq, comparator_15_eq, comparator_16_eq);

  // Notes on the sheet:
  //   ALARMA  ENCENDIDA
endmodule

module DecoLED (
  input  I4,
  input  I3,
  input  I2,
  input  I1,
  output o1,
  output o2,
  output o3,
  output o5,
  output o6,
  output o7,
  output o8
);

  wire and_1_out, and_2_out, and_3_out, and_4_out, and_5_out, and_6_out, and_7_out, and_8_out, and_9_out,
       and_10_out, and_11_out, and_12_out, and_13_out, and_14_out, and_15_out, and_16_out, and_17_out,
       and_18_out, and_19_out, and_20_out, and_21_out, and_22_out, and_23_out, and_24_out, and_25_out,
       and_26_out, and_27_out, and_28_out, and_29_out, and_30_out, and_31_out, and_32_out, and_33_out,
       and_34_out, and_35_out, and_36_out, not_1_out, not_2_out, not_3_out, not_4_out, not_5_out, not_6_out,
       not_7_out, not_8_out, not_9_out, not_10_out, not_11_out, not_12_out, not_13_out, not_14_out,
       not_15_out, not_16_out, not_17_out, not_18_out, not_19_out, not_20_out, not_21_out, not_22_out,
       not_23_out, not_24_out, not_25_out, not_26_out, not_27_out, not_28_out, not_29_out, not_30_out,
       not_31_out, not_32_out, not_33_out, not_34_out, not_35_out, not_36_out, not_37_out, not_38_out,
       not_39_out, not_40_out, not_41_out, not_42_out, not_43_out, not_44_out, not_45_out;

  not not_1 (not_1_out, I3);
  and and_1 (and_1_out, not_1_out, not_2_out);
  not not_2 (not_2_out, I1);
  and and_2 (and_2_out, I2, not_3_out);
  not not_3 (not_3_out, I1);
  and and_3 (and_3_out, I4, I2);
  and and_4 (and_4_out, I4, I3);
  not not_4 (not_4_out, I3);
  not not_5 (not_5_out, I2);
  and and_5 (and_5_out, not_4_out, not_5_out, not_6_out);
  not not_6 (not_6_out, I1);
  not not_7 (not_7_out, I4);
  and and_6 (and_6_out, not_7_out, I2, not_8_out);
  not not_8 (not_8_out, I1);
  not not_9 (not_9_out, I3);
  and and_7 (and_7_out, not_9_out, I2, I1);
  and and_8 (and_8_out, I3, not_10_out, I1);
  not not_10 (not_10_out, I2);
  and and_9 (and_9_out, I4, I3, not_11_out);
  not not_11 (not_11_out, I1);
  not not_12 (not_12_out, I3);
  and and_10 (and_10_out, not_12_out, not_13_out);
  not not_13 (not_13_out, I2);
  not not_14 (not_14_out, I3);
  and and_11 (and_11_out, not_14_out, I1);
  not not_15 (not_15_out, I2);
  and and_12 (and_12_out, not_15_out, I1);
  not not_16 (not_16_out, I4);
  and and_13 (and_13_out, not_16_out, I3);
  and and_14 (and_14_out, I4, not_17_out);
  not not_17 (not_17_out, I3);
  not not_18 (not_18_out, I3);
  and and_15 (and_15_out, not_18_out, I2);
  and and_16 (and_16_out, I2, not_19_out);
  not not_19 (not_19_out, I1);
  not not_20 (not_20_out, I4);
  and and_17 (and_17_out, not_20_out, I3, not_21_out);
  not not_21 (not_21_out, I1);
  not not_22 (not_22_out, I2);
  and and_18 (and_18_out, I3, not_22_out, I1);
  and and_19 (and_19_out, I4, not_23_out);
  not not_23 (not_23_out, I3);
  and and_20 (and_20_out, I4, I2);
  not not_24 (not_24_out, I2);
  and and_21 (and_21_out, not_24_out, not_25_out);
  not not_25 (not_25_out, I1);
  not not_26 (not_26_out, I4);
  and and_22 (and_22_out, not_26_out, I3, not_27_out);
  not not_27 (not_27_out, I2);
  and and_23 (and_23_out, I3, not_28_out);
  not not_28 (not_28_out, I1);
  and and_24 (and_24_out, I4, not_29_out);
  not not_29 (not_29_out, I3);
  and and_25 (and_25_out, I4, I2);
  not not_30 (not_30_out, I3);
  and and_26 (and_26_out, not_30_out, not_31_out);
  not not_31 (not_31_out, I1);
  not not_32 (not_32_out, I4);
  and and_27 (and_27_out, not_32_out, I2, I1);
  not not_33 (not_33_out, I4);
  and and_28 (and_28_out, not_33_out, I3, I1);
  and and_29 (and_29_out, I3, I2, I1);
  and and_30 (and_30_out, I4, not_34_out, not_35_out);
  not not_34 (not_34_out, I3);
  not not_35 (not_35_out, I2);
  and and_31 (and_31_out, I4, not_36_out);
  not not_36 (not_36_out, I1);
  not not_37 (not_37_out, I4);
  not not_38 (not_38_out, I2);
  and and_32 (and_32_out, not_37_out, not_38_out, not_39_out);
  not not_39 (not_39_out, I1);
  not not_40 (not_40_out, I3);
  and and_33 (and_33_out, not_40_out, not_41_out);
  not not_41 (not_41_out, I2);
  not not_42 (not_42_out, I3);
  and and_34 (and_34_out, not_42_out, not_43_out);
  not not_43 (not_43_out, I1);
  not not_44 (not_44_out, I4);
  and and_35 (and_35_out, not_44_out, I2, I1);
  and and_36 (and_36_out, I4, not_45_out, I1);
  not not_45 (not_45_out, I2);
  or or_1 (o1, and_1_out, and_2_out, and_3_out, and_4_out);
  or or_2 (o2, and_5_out, and_6_out, and_7_out, and_8_out, and_9_out);
  or or_3 (o3, and_10_out, and_11_out, and_12_out, and_13_out, and_14_out);
  or or_4 (o6, and_21_out, and_22_out, and_23_out, and_24_out, and_25_out);
  or or_5 (o8, and_32_out, and_33_out, and_34_out, and_35_out, and_36_out);
  or or_6 (o5, and_15_out, and_16_out, and_17_out, and_18_out, and_19_out, and_20_out);
  or or_7 (o7, and_26_out, and_27_out, and_28_out, and_29_out, and_30_out, and_31_out);
endmodule

module Cont4Bit (
  input  T,
  input  Reset,
  output Q3,
  output Q2,
  output Q1,
  output Q0
);

  wire t_ff_1_qn, t_ff_2_qn, t_ff_3_qn;

  T_Flip_Flop t_ff_1 (.clk(T), .T(1'b1), .Q(Q0), .Qn(t_ff_1_qn), .reset(Reset));  // open: preset, en
  T_Flip_Flop t_ff_2 (.clk(t_ff_1_qn), .T(1'b1), .Q(Q1), .Qn(t_ff_2_qn), .reset(Reset));  // open: preset, en
  T_Flip_Flop t_ff_3 (.clk(t_ff_2_qn), .T(1'b1), .Q(Q2), .Qn(t_ff_3_qn), .reset(Reset));  // open: preset, en
  T_Flip_Flop t_ff_4 (.clk(t_ff_3_qn), .T(1'b1), .Q(Q3), .reset(Reset));  // open: Qn, preset, en
endmodule
