// Logisim project Reloj&Alarma (1).circ as structural Verilog: 15 circuits, main circuit main
module main (
);

  wire _1, _2, _3, _4, _5, _6, _7, _8, _9, _10, _11, _12, _13, _14, _15, _16, _17, _18, _19, _20, _21, _22,
       _23, _24, _25, _26, _27, _28, _29, _30, _31, _32, _33, _34, _35, _36, _37, _38, _39, _40, _41, _42,
       Alarma, Control_Reloj, Display_Alarma, Hora_Alarma, Hora_Reloj, Hora_Reloj2, Hrs_out, M_out,
       Minutos_Alarma, Minutos_Reloj, Minutos_Reloj2, Mts_out, Reloj_en_pausa, Reloj_out, tunnel;

  _7_Segment_Display u_7_segment_display_1 (.g(_39), .f(_40), .a(_41), .b(_42), .e(_36), .d(_37), .c(_38));  // open: dp
  _7_Segment_Display u_7_segment_display_2 (.g(_32), .f(_33), .a(_34), .b(_35), .e(_29), .d(_30), .c(_31));  // open: dp
  Button M (.out(M_out));
  Button Hrs (.out(Hrs_out));
  Button Mts (.out(Mts_out));
  Reloj_Alarma reloj_alarma_1 (
    .out_21(_36), .out_22(_37), .out_23(_38), .out_24(_39), .out_25(_40), .out_26(_41), .out_27(_42),
    .out_7(_29), .out_8(_30), .out_9(_31), .out_10(_32), .out_11(_33), .out_12(_34), .out_13(_35),
    .out_14(_22), .out_15(_23), .out_35(_8), .out_16(_24), .out_36(_9), .out_17(_25), .out_37(_10),
    .out_18(_26), .out_38(_11), .out_19(_27), .out_39(_12), .out_20(_28), .out_40(_13), .out_41(_14),
    .out_28(_15), .out_42(_1), .out_29(_16), .out_43(_2), .out_30(_17), .out_44(_3), .out_31(_18),
    .out_45(_4), .out_32(_19), .out_46(_5), .out_33(_20), .out_47(_6), .out_34(_21), .out_48(_7),
    .out_49(Alarma), .in_4(Hora_Reloj2), .in_5(Minutos_Reloj2), .in_6(tunnel), .in_1(Hora_Alarma),
    .in_2(Minutos_Alarma), .in_3(Display_Alarma));
  LED led_1 (.in(tunnel));
  _7_Segment_Display u_7_segment_display_3 (.g(_25), .f(_26), .a(_27), .b(_28), .e(_22), .d(_23), .c(_24));  // open: dp
  LED led_2 (.in(tunnel));
  switch switch_1 (.in_1(M_out), .out_2(Display_Alarma), .out_3(Control_Reloj));
  Botones botones_1 (
    .in_1(Hrs_out), .in_2(Control_Reloj), .in_3(Display_Alarma), .out_4(Hora_Reloj), .out_5(Hora_Alarma));
  Botones botones_2 (
    .in_1(Mts_out), .in_2(Control_Reloj), .in_3(Display_Alarma), .out_4(Minutos_Reloj), .out_5(Minutos_Alarma));
  _7_Segment_Display u_7_segment_display_4 (.g(_18), .f(_19), .a(_20), .b(_21), .e(_15), .d(_16), .c(_17));  // open: dp
  LED led_3 (.in(tunnel));
  LED led_4 (.in(tunnel));
  _7_Segment_Display u_7_segment_display_5 (.g(_11), .f(_12), .a(_13), .b(_14), .e(_8), .d(_9), .c(_10));  // open: dp
  _7_Segment_Display u_7_segment_display_6 (.g(_4), .f(_5), .a(_6), .b(_7), .e(_1), .d(_2), .c(_3));  // open: dp
  switch switch_2 (.in_1(Control_Reloj), .out_2(Reloj_en_pausa));  // open: out_3
  and and_1 (Hora_Reloj2, Reloj_en_pausa, Hora_Reloj);
  and and_2 (Minutos_Reloj2, Reloj_en_pausa, Minutos_Reloj);
  Multiplexer multiplexer_1 (.in0(Reloj_out), .in1(1'b0), .out(tunnel), .sel(Reloj_en_pausa), .en(1'b1));
  LED led_5 (.in(Reloj_en_pausa));
  LED led_6 (.in(Display_Alarma));
  LED led_7 (.in(Control_Reloj));
  Clock Reloj (.out(Reloj_out));
  LED Alarma_Sonando (.in(Alarma));

  // Other names for the same wires on the sheet: ModoAlarma = Display_Alarma; ModoReloj = Control_Reloj

  // Notes on the sheet:
  //   Control Horas
  //   Control Minutos
  //   Hora
  //   Control Modo
  //   Minutos
  //   e
  //   e
  //   Segundos
  //   e
  //   RELOJ EN PAUSA
  //   MODO ALARMA
  //   MODO RELOJ
endmodule

module cont4Bit (
  input  T,
  input  Reset,
  output Q3,
  output Q2,
  output Q1,
  output Q0
);

  wire t_ff_1_qn, t_ff_2_qn, t_ff_3_qn;

  T_Flip_Flop t_ff_1 (.clk(T), .T(1'b1), .Q(Q0), .Qn(t_ff_1_qn), .reset(Reset));  // open: preset, en
  T_Flip_Flop t_ff_2 (.clk(t_ff_1_qn), .T(1'b1), .Q(Q1), .Qn(t_ff_2_qn), .reset(Reset));  // open: preset, en
  T_Flip_Flop t_ff_3 (.clk(t_ff_2_qn), .T(1'b1), .Q(Q2), .Qn(t_ff_3_qn), .reset(Reset));  // open: preset, en
  T_Flip_Flop t_ff_4 (.clk(t_ff_3_qn), .T(1'b1), .Q(Q3), .reset(Reset));  // open: Qn, preset, en
endmodule

module DecoLED (
  input  I4,
  input  I3,
  input  I2,
  input  I1,
  output o1,
  output o2,
  output o3,
  output o5,
  output o6,
  output o7,
  output o8
);

  wire and_1_out, and_2_out, and_3_out, and_4_out, and_5_out, and_6_out, and_7_out, and_8_out, and_9_out,
       and_10_out, and_11_out, and_12_out, and_13_out, and_14_out, and_15_out, and_16_out, and_17_out,
       and_18_out, and_19_out, and_20_out, and_21_out, and_22_out, and_23_out, and_24_out, and_25_out,
       and_26_out, and_27_out, and_28_out, and_29_out, and_30_out, and_31_out, and_32_out, and_33_out,
       and_34_out, and_35_out, and_36_out, not_1_out, not_2_out, not_3_out, not_4_out, not_5_out, not_6_out,
       not_7_out, not_8_out, not_9_out, not_10_out, not_11_out, not_12_out, not_13_out, not_14_out,
       not_15_out, not_16_out, not_17_out, not_18_out, not_19_out, not_20_out, not_21_out, not_22_out,
       not_23_out, not_24_out, not_25_out, not_26_out, not_27_out, not_28_out, not_29_out, not_30_out,
       not_31_out, not_32_out, not_33_out, not_34_out, not_35_out, not_36_out, not_37_out, not_38_out,
       not_39_out, not_40_out, not_41_out, not_42_out, not_43_out, not_44_out, not_45_out;

  not not_1 (not_1_out, I3);
  and and_1 (and_1_out, not_1_out, not_2_out);
  not not_2 (not_2_out, I1);
  and and_2 (and_2_out, I2, not_3_out);
  not not_3 (not_3_out, I1);
  and and_3 (and_3_out, I4, I2);
  and and_4 (and_4_out, I4, I3);
  not not_4 (not_4_out, I3);
  and and_5 (and_5_out, not_4_out, not_5_out, not_6_out);
  not not_5 (not_5_out, I2);
  not not_6 (not_6_out, I1);
  not not_7 (not_7_out, I4);
  and and_6 (and_6_out, not_7_out, I2, not_8_out);
  not not_8 (not_8_out, I1);
  not not_9 (not_9_out, I3);
  and and_7 (and_7_out, not_9_out, I2, I1);
  not not_10 (not_10_out, I2);
  and and_8 (and_8_out, I3, not_10_out, I1);
  and and_9 (and_9_out, I4, I3, not_11_out);
  not not_11 (not_11_out, I1);
  not not_12 (not_12_out, I3);
  and and_10 (and_10_out, not_12_out, not_13_out);
  not not_13 (not_13_out, I2);
  not not_14 (not_14_out, I3);
  and and_11 (and_11_out, not_14_out, I1);
  not not_15 (not_15_out, I2);
  and and_12 (and_12_out, not_15_out, I1);
  not not_16 (not_16_out, I4);
  and and_13 (and_13_out, not_16_out, I3);
  and and_14 (and_14_out, I4, not_17_out);
  not not_17 (not_17_out, I3);
  not not_18 (not_18_out, I3);
  and and_15 (and_15_out, not_18_out, I2);
  and and_16 (and_16_out, I2, not_19_out);
  not not_19 (not_19_out, I1);
  not not_20 (not_20_out, I4);
  and and_17 (and_17_out, not_20_out, I3, not_21_out);
  not not_21 (not_21_out, I1);
  and and_18 (and_18_out, I3, not_22_out, I1);
  not not_22 (not_22_out, I2);
  and and_19 (and_19_out, I4, not_23_out);
  not not_23 (not_23_out, I3);
  and and_20 (and_20_out, I4, I2);
  not not_24 (not_24_out, I2);
  and and_21 (and_21_out, not_24_out, not_25_out);
  not not_25 (not_25_out, I1);
  not not_26 (not_26_out, I4);
  and and_22 (and_22_out, not_26_out, I3, not_27_out);
  not not_27 (not_27_out, I2);
  and and_23 (and_23_out, I3, not_28_out);
  not not_28 (not_28_out, I1);
  and and_24 (and_24_out, I4, not_29_out);
  not not_29 (not_29_out, I3);
  and and_25 (and_25_out, I4, I2);
  not not_30 (not_30_out, I3);
  and and_26 (and_26_out, not_30_out, not_31_out);
  not not_31 (not_31_out, I1);
  not not_32 (not_32_out, I4);
  and and_27 (and_27_out, not_32_out, I2, I1);
  not not_33 (not_33_out, I4);
  and and_28 (and_28_out, not_33_out, I3, I1);
  and and_29 (and_29_out, I3, I2, I1);
  and and_30 (and_30_out, I4, not_34_out, not_35_out);
  not not_34 (not_34_out, I3);
  not not_35 (not_35_out, I2);
  and and_31 (and_31_out, I4, not_36_out);
  not not_36 (not_36_out, I1);
  not not_37 (not_37_out, I4);
  not not_38 (not_38_out, I2);
  and and_32 (and_32_out, not_37_out, not_38_out, not_39_out);
  not not_39 (not_39_out, I1);
  not not_40 (not_40_out, I3);
  and and_33 (and_33_out, not_40_out, not_41_out);
  not not_41 (not_41_out, I2);
  not not_42 (not_42_out, I3);
  and and_34 (and_34_out, not_42_out, not_43_out);
  not not_43 (not_43_out, I1);
  not not_44 (not_44_out, I4);
  and and_35 (and_35_out, not_44_out, I2, I1);
  not not_45 (not_45_out, I2);
  and and_36 (and_36_out, I4, not_45_out, I1);
  or or_1 (o1, and_1_out, and_2_out, and_3_out, and_4_out);
  or or_2 (o2, and_5_out, and_6_out, and_7_out, and_8_out, and_9_out);
  or or_3 (o3, and_10_out, and_11_out, and_12_out, and_13_out, and_14_out);
  or or_4 (o6, and_21_out, and_22_out, and_23_out, and_24_out, and_25_out);
  or or_5 (o8, and_32_out, and_33_out, and_34_out, and_35_out, and_36_out);
  or or_6 (o5, and_15_out, and_16_out, and_17_out, and_18_out, and_19_out, and_20_out);
  or or_7 (o7, and_26_out, and_27_out, and_28_out, and_29_out, and_30_out, and_31_out);
endmodule

module muxDisplay7Seg (
  input  in_1,
  input  in_2,
  input  in_3,
  input  in_4,
  input  in_5,
  input  in_6,
  input  in_7,
  input  in_8,
  input  in_9,
  input  in_10,
  input  in_11,
  input  in_12,
  input  in_13,
  input  in_14,
  input  in_15,
  output out_16,
  output out_17,
  output out_18,
  output out_19,
  output out_20,
  output out_21,
  output out_22
);

  muxDisplaySelector muxdisplayselector_1 (.in_1(in_1), .in_2(in_2), .in_3(in_3), .out_4(out_16));
  muxDisplaySelector muxdisplayselector_2 (.in_1(in_1), .in_2(in_4), .in_3(in_5), .out_4(out_17));
  muxDisplaySelector muxdisplayselector_3 (.in_1(in_1), .in_2(in_6), .in_3(in_7), .out_4(out_18));
  muxDisplaySelector muxdisplayselector_4 (.in_1(in_1), .in_2(in_8), .in_3(in_9), .out_4(out_19));
  muxDisplaySelector muxdisplayselector_5 (.in_1(in_1), .in_2(in_10), .in_3(in_11), .out_4(out_20));
  muxDisplaySelector muxdisplayselector_6 (.in_1(in_1), .in_2(in_12), .in_3(in_13), .out_4(out_21));
  muxDisplaySelector muxdisplayselector_7 (.in_1(in_1), .in_2(in_14), .in_3(in_15), .out_4(out_22));
endmodule

module muxDisplaySelector (
  input  in_1,
  input  in_2,
  input  in_3,
  output out_4
);

  wire and_1_out, and_2_out, not_1_out;

  not not_1 (not_1_out, in_1);
  and and_1 (and_1_out, not_1_out, in_2);
  and and_2 (and_2_out, in_1, in_3);
  or or_1 (out_4, and_1_out, and_2_out);
endmodule

module Comparador (
  input  A,
  input  a_2,
  input  B,
  input  b_2,
  input  C,
  input  c_2,
  input  D,
  input  d_2,
  input  E,
  input  e_2,
  input  F,
  input  f_2,
  input  G,
  input  g_2,
  input  H,
  input  h_2,
  input  I,
  input  i_2,
  input  J,
  input  j_2,
  input  K,
  input  k_2,
  input  L,
  input  l_2,
  input  M,
  input  m_2,
  input  N,
  input  n_2,
  input  O,
  input  o_2,
  input  P,
  input  p_2,
  output out_33
);

  wire comparator_1_eq, comparator_2_eq, comparator_3_eq, comparator_4_eq, comparator_5_eq, comparator_6_eq,
       comparator_7_eq, comparator_8_eq, comparator_9_eq, comparator_10_eq, comparator_11_eq,
       comparator_12_eq, comparator_13_eq, comparator_14_eq, comparator_15_eq, comparator_16_eq;

  Comparator #(.width(1)) comparator_1 (.a(A), .b(a_2), .eq(comparator_1_eq));  // open: gt, lt
  Comparator #(.width(1)) comparator_2 (.a(B), .b(b_2), .eq(comparator_2_eq));  // open: gt, lt
  Comparator #(.width(1)) comparator_3 (.a(C), .b(c_2), .eq(comparator_3_eq));  // open: gt, lt
  Comparator #(.width(1)) comparator_4 (.a(D), .b(d_2), .eq(comparator_4_eq));  // open: gt, lt
  Comparator #(.width(1)) comparator_5 (.a(E), .b(e_2), .eq(comparator_5_eq));  // open: gt, lt
  Comparator #(.width(1)) comparator_6 (.a(F), .b(f_2), .eq(comparator_6_eq));  // open: gt, lt
  Comparator #(.width(1)) comparator_7 (.a(G), .b(g_2), .eq(comparator_7_eq));  // open: gt, lt
  Comparator #(.width(1)) comparator_8 (.a(H), .b(h_2), .eq(comparator_8_eq));  // open: gt, lt
  Comparator #(.width(1)) comparator_9 (.a(I), .b(i_2), .eq(comparator_9_eq));  // open: gt, lt
  Comparator #(.width(1)) comparator_10 (.a(J), .b(j_2), .eq(comparator_10_eq));  // open: gt, lt
  Comparator #(.width(1)) comparator_11 (.a(K), .b(k_2), .eq(comparator_11_eq));  // open: gt, lt
  Comparator #(.width(1)) comparator_12 (.a(L), .b(l_2), .eq(comparator_12_eq));  // open: gt, lt
  Comparator #(.width(1)) comparator_13 (.a(M), .b(m_2), .eq(comparator_13_eq));  // open: gt, lt
  Comparator #(.width(1)) comparator_14 (.a(N), .b(n_2), .eq(comparator_14_eq));  // open: gt, lt
  Comparator #(.width(1)) comparator_15 (.a(O), .b(o_2), .eq(comparator_15_eq));  // open: gt, lt
  Comparator #(.width(1)) comparator_16 (.a(P), .b(p_2), .eq(comparator_16_eq));  // open: gt, lt
  and and_1 (out_33, comparator_1_eq, comparator_2_eq, comparator_3_eq, comparator_4_eq, comparator_5_eq, comparator_6_eq, comparator_7_eq, comparator_8_eq, comparator_9_eq, comparator_10_eq, comparator_11_eq, comparator_12_eq, comparator_13_eq, comparator_14_eq, comparator_15_eq, comparator_16_eq);

  // Notes on the sheet:
  //   ALARMA  ENCENDIDA
endmodule

module alarma (
  input  in_1,
  input  in_2,
  output out_3,
  output out_4,
  output out_5,
  output out_6,
  output out_7,
  output out_8,
  output out_9,
  output out_10,
  output out_11,
  output out_12,
  output out_13,
  output out_14,
  output out_15,
  output out_16,
  output out_17,
  output out_18,
  output out_19,
  output out_20,
  output out_21,
  output out_22,
  output out_23,
  output out_24,
  output out_25,
  output out_26,
  output out_27,
  output out_28,
  output out_29,
  output out_30,
  output _2_3,
  output _2_3_2,
  output _2_2,
  output _2_3_3,
  output _2_3_4,
  output _2_2_2,
  output _2_1,
  output _2_2_3,
  output _2_1_2,
  output _2_2_4,
  output _2_0,
  output _2_1_3,
  output _2_0_2,
  output _2_1_4,
  output _2_0_3,
  output _2_0_4
);

  wire and_1_out, and_2_out, and_3_out, and_4_out, or_1_out, or_2_out;

  DecoLED decoled_1 (
    .I4(_2_3_4), .I3(_2_2_4), .I2(_2_1_4), .I1(_2_0_4), .o1(out_21), .o2(out_15), .o3(out_4), .o5(out_3),
    .o6(out_5), .o7(out_16), .o8(out_24));
  cont4Bit cont4bit_1 (.T(and_2_out), .Reset(and_1_out), .Q3(_2_3_4), .Q2(_2_2_4), .Q1(_2_1_4), .Q0(_2_0_4));
  and and_1 (and_1_out, _2_2, _2_1_4);
  and and_2 (and_2_out, _2_3, _2_1);
  or or_1 (or_1_out, and_2_out, and_1_out);
  DecoLED decoled_2 (
    .I4(_2_3), .I3(_2_2), .I2(_2_1), .I1(_2_0), .o1(out_25), .o2(out_17), .o3(out_7), .o5(out_6), .o6(out_8),
    .o7(out_18), .o8(out_26));
  cont4Bit cont4bit_2 (.T(or_2_out), .Reset(or_1_out), .Q3(_2_3), .Q2(_2_2), .Q1(_2_1), .Q0(_2_0));
  or or_2 (or_2_out, and_3_out, in_2);
  DecoLED decoled_3 (
    .I4(_2_3_2), .I3(_2_2_2), .I2(_2_1_2), .I1(_2_0_2), .o1(out_27), .o2(out_19), .o3(out_10), .o5(out_9),
    .o6(out_11), .o7(out_20), .o8(out_28));
  cont4Bit cont4bit_3 (.T(and_4_out), .Reset(and_3_out), .Q3(_2_3_2), .Q2(_2_2_2), .Q1(_2_1_2), .Q0(_2_0_2));
  and and_3 (and_3_out, _2_2_2, _2_1_2);
  and and_4 (and_4_out, _2_3_3, _2_1_3);
  DecoLED decoled_4 (
    .I4(_2_3_3), .I3(_2_2_3), .I2(_2_1_3), .I1(_2_0_3), .o1(out_29), .o2(out_22), .o3(out_13), .o5(out_12),
    .o6(out_14), .o7(out_23), .o8(out_30));
  cont4Bit cont4bit_4 (.T(in_1), .Reset(and_4_out), .Q3(_2_3_3), .Q2(_2_2_3), .Q1(_2_1_3), .Q0(_2_0_3));
endmodule

module reloj (
  input  in_1,
  input  in_2,
  input  in_3,
  output out_4,
  output out_5,
  output out_6,
  output out_7,
  output out_8,
  output out_9,
  output out_10,
  output out_11,
  output out_12,
  output out_13,
  output out_14,
  output out_15,
  output out_16,
  output out_17,
  output out_18,
  output out_19,
  output out_20,
  output out_21,
  output out_22,
  output out_23,
  output out_24,
  output out_25,
  output out_26,
  output out_27,
  output out_28,
  output out_29,
  output out_30,
  output out_31,
  output out_32,
  output out_33,
  output out_34,
  output out_35,
  output out_36,
  output out_37,
  output out_38,
  output out_39,
  output out_40,
  output out_41,
  output out_42,
  output out_43,
  output out_44,
  output out_45,
  output _2_3,
  output _2_3_2,
  output _2_3_3,
  output _2_3_4,
  output _2_2,
  output _2_2_2,
  output _2_2_3,
  output _2_3_5,
  output _2_3_6,
  output _2_2_4,
  output _2_1,
  output _2_1_2,
  output _2_1_3,
  output _2_2_5,
  output _2_1_4,
  output _2_0,
  output _2_0_2,
  output _2_2_6,
  output _2_0_3,
  output _2_1_5,
  output _2_0_4,
  output _2_1_6,
  output _2_0_5,
  output _2_0_6
);

  wire and_1_out, and_2_out, and_3_out, and_4_out, and_5_out, and_6_out, or_1_out, or_2_out, or_3_out;

  and and_1 (and_1_out, _2_2_3, _2_1_6);
  DecoLED decoled_1 (
    .I4(_2_3_6), .I3(_2_2_6), .I2(_2_1_6), .I1(_2_0_6), .o1(out_33), .o2(out_24), .o3(out_9), .o5(out_5),
    .o6(out_10), .o7(out_25), .o8(out_38));
  cont4Bit cont4bit_1 (.T(and_2_out), .Reset(and_1_out), .Q3(_2_3_6), .Q2(_2_2_6), .Q1(_2_1_6), .Q0(_2_0_6));
  DecoLED decoled_2 (
    .I4(_2_3_3), .I3(_2_2_3), .I2(_2_1_3), .I1(_2_0_3), .o1(out_39), .o2(out_28), .o3(out_14), .o5(out_11),
    .o6(out_15), .o7(out_29), .o8(out_41));
  and and_2 (and_2_out, _2_3_3, _2_1_3);
  cont4Bit cont4bit_2 (.T(or_2_out), .Reset(or_1_out), .Q3(_2_3_3), .Q2(_2_2_3), .Q1(_2_1_3), .Q0(_2_0_3));
  or or_1 (or_1_out, and_2_out, and_1_out);
  or or_2 (or_2_out, and_3_out, in_3);
  and and_3 (and_3_out, _2_2_4, _2_1_4);
  DecoLED decoled_3 (
    .I4(_2_3_4), .I3(_2_2_4), .I2(_2_1_4), .I1(_2_0_4), .o1(out_42), .o2(out_30), .o3(out_17), .o5(out_16),
    .o6(out_18), .o7(out_31), .o8(out_43));
  cont4Bit cont4bit_3 (.T(and_4_out), .Reset(and_3_out), .Q3(_2_3_4), .Q2(_2_2_4), .Q1(_2_1_4), .Q0(_2_0_4));
  and and_4 (and_4_out, _2_3_5, _2_1_5);
  DecoLED decoled_4 (
    .I4(_2_3_5), .I3(_2_2_5), .I2(_2_1_5), .I1(_2_0_5), .o1(out_44), .o2(out_34), .o3(out_20), .o5(out_19),
    .o6(out_21), .o7(out_35), .o8(out_45));
  cont4Bit cont4bit_4 (.T(or_3_out), .Reset(and_4_out), .Q3(_2_3_5), .Q2(_2_2_5), .Q1(_2_1_5), .Q0(_2_0_5));
  or or_3 (or_3_out, and_5_out, in_2);
  and and_5 (and_5_out, _2_2, _2_1);
  DecoLED decoled_5 (
    .I4(_2_3), .I3(_2_2), .I2(_2_1), .I1(_2_0), .o1(out_32), .o2(out_22), .o3(out_6), .o5(out_4), .o6(out_7),
    .o7(out_23), .o8(out_36));
  cont4Bit cont4bit_5 (.T(and_6_out), .Reset(and_5_out), .Q3(_2_3), .Q2(_2_2), .Q1(_2_1), .Q0(_2_0));
  and and_6 (and_6_out, _2_3_2, _2_1_2);
  DecoLED decoled_6 (
    .I4(_2_3_2), .I3(_2_2_2), .I2(_2_1_2), .I1(_2_0_2), .o1(out_37), .o2(out_26), .o3(out_12), .o5(out_8),
    .o6(out_13), .o7(out_27), .o8(out_40));
  cont4Bit cont4bit_6 (.T(in_1), .Reset(and_6_out), .Q3(_2_3_2), .Q2(_2_2_2), .Q1(_2_1_2), .Q0(_2_0_2));
endmodule

module Mux4Displays7Seg (
  input  in_1,
  input  in_2,
  input  in_3,
  input  in_4,
  input  in_5,
  input  in_6,
  input  in_7,
  input  in_8,
  input  in_9,
  input  in_10,
  input  in_11,
  input  in_12,
  input  in_13,
  input  in_14,
  input  in_15,
  input  in_16,
  input  in_17,
  input  in_18,
  input  in_19,
  input  in_20,
  input  in_21,
  input  in_22,
  input  in_23,
  input  in_24,
  input  in_25,
  input  in_26,
  input  in_27,
  input  in_28,
  input  in_29,
  input  in_30,
  input  in_31,
  input  in_32,
  input  in_33,
  input  in_34,
  input  in_35,
  input  in_36,
  input  in_37,
  input  in_38,
  input  in_39,
  input  in_40,
  input  in_41,
  input  in_42,
  input  in_43,
  input  in_44,
  input  in_45,
  input  in_46,
  input  in_47,
  input  in_48,
  input  in_49,
  input  in_50,
  input  in_51,
  input  in_52,
  input  in_53,
  input  in_54,
  input  in_55,
  input  in_56,
  input  in_57,
  output out_58,
  output out_59,
  output out_60,
  output out_61,
  output out_62,
  output out_63,
  output out_64,
  output out_65,
  output out_66,
  output out_67,
  output out_68,
  output out_69,
  output out_70,
  output out_71,
  output out_72,
  output out_73,
  output out_74,
  output out_75,
  output out_76,
  output out_77,
  output out_78,
  output out_79,
  output out_80,
  output out_81,
  output out_82,
  output out_83,
  output out_84,
  output out_85
);

  muxDisplay7Seg muxdisplay7seg_1 (
    .in_1(in_1), .in_2(in_2), .in_3(in_3), .in_4(in_4), .in_5(in_5), .in_6(in_6), .in_7(in_7), .in_8(in_8),
    .in_9(in_9), .in_10(in_10), .in_11(in_11), .in_12(in_12), .in_13(in_13), .in_14(in_14), .in_15(in_15),
    .out_16(out_58), .out_17(out_59), .out_18(out_60), .out_19(out_61), .out_20(out_62), .out_21(out_63),
    .out_22(out_64));
  muxDisplay7Seg muxdisplay7seg_2 (
    .in_1(in_1), .in_2(in_16), .in_3(in_17), .in_4(in_18), .in_5(in_19), .in_6(in_20), .in_7(in_21),
    .in_8(in_22), .in_9(in_23), .in_10(in_24), .in_11(in_25), .in_12(in_26), .in_13(in_27), .in_14(in_28),
    .in_15(in_29), .out_16(out_65), .out_17(out_66), .out_18(out_67), .out_19(out_68), .out_20(out_69),
    .out_21(out_70), .out_22(out_71));
  muxDisplay7Seg muxdisplay7seg_3 (
    .in_1(in_1), .in_2(in_30), .in_3(in_31), .in_4(in_32), .in_5(in_33), .in_6(in_34), .in_7(in_35),
    .in_8(in_36), .in_9(in_37), .in_10(in_38), .in_11(in_39), .in_12(in_40), .in_13(in_41), .in_14(in_42),
    .in_15(in_43), .out_16(out_72), .out_17(out_73), .out_18(out_74), .out_19(out_75), .out_20(out_76),
    .out_21(out_77), .out_22(out_78));
  muxDisplay7Seg muxdisplay7seg_4 (
    .in_1(in_1), .in_2(in_44), .in_3(in_45), .in_4(in_46), .in_5(in_47), .in_6(in_48), .in_7(in_49),
    .in_8(in_50), .in_9(in_51), .in_10(in_52), .in_11(in_53), .in_12(in_54), .in_13(in_55), .in_14(in_56),
    .in_15(in_57), .out_16(out_79), .out_17(out_80), .out_18(out_81), .out_19(out_82), .out_20(out_83),
    .out_21(out_84), .out_22(out_85));
endmodule

module Reloj_Alarma (
  input  in_1,
  input  in_2,
  input  in_3,
  input  in_4,
  input  in_5,
  input  in_6,
  output out_7,
  output out_8,
  output out_9,
  output out_10,
  output out_11,
  output out_12,
  output out_13,
  output out_14,
  output out_15,
  output out_16,
  output out_17,
  output out_18,
  output out_19,
  output out_20,
  output out_21,
  output out_22,
  output out_23,
  output out_24,
  output out_25,
  output out_26,
  output out_27,
  output out_28,
  output out_29,
  output out_30,
  output out_31,
  output out_32,
  output out_33,
  output out_34,
  output out_35,
  output out_36,
  output out_37,
  output out_38,
  output out_39,
  output out_40,
  output out_41,
  output out_42,
  output out_43,
  output out_44,
  output out_45,
  output out_46,
  output out_47,
  output out_48,
  output out_49
);

  wire alarma_1__2_0, alarma_1__2_0_2, alarma_1__2_0_3, alarma_1__2_0_4, alarma_1__2_1, alarma_1__2_1_2,
       alarma_1__2_1_3, alarma_1__2_1_4, alarma_1__2_2, alarma_1__2_2_2, alarma_1__2_2_3, alarma_1__2_2_4,
       alarma_1__2_3, alarma_1__2_3_2, alarma_1__2_3_3, alarma_1__2_3_4, alarma_1_out_3, alarma_1_out_4,
       alarma_1_out_5, alarma_1_out_6, alarma_1_out_7, alarma_1_out_8, alarma_1_out_9, alarma_1_out_10,
       alarma_1_out_11, alarma_1_out_12, alarma_1_out_13, alarma_1_out_14, alarma_1_out_15, alarma_1_out_16,
       alarma_1_out_17, alarma_1_out_18, alarma_1_out_19, alarma_1_out_20, alarma_1_out_21, alarma_1_out_22,
       alarma_1_out_23, alarma_1_out_24, alarma_1_out_25, alarma_1_out_26, alarma_1_out_27, alarma_1_out_28,
       alarma_1_out_29, alarma_1_out_30, c1, c2, c3, c4, c5, c6, c7, c8, n20seg_1_out_11, reloj_1__2_0_3,
       reloj_1__2_0_4, reloj_1__2_0_5, reloj_1__2_0_6, reloj_1__2_1_3, reloj_1__2_1_4, reloj_1__2_1_5,
       reloj_1__2_1_6, reloj_1__2_2_3, reloj_1__2_2_4, reloj_1__2_2_5, reloj_1__2_2_6, reloj_1__2_3_3,
       reloj_1__2_3_4, reloj_1__2_3_5, reloj_1__2_3_6, reloj_1_out_5, reloj_1_out_9, reloj_1_out_10,
       reloj_1_out_11, reloj_1_out_14, reloj_1_out_15, reloj_1_out_16, reloj_1_out_17, reloj_1_out_18,
       reloj_1_out_19, reloj_1_out_20, reloj_1_out_21, reloj_1_out_24, reloj_1_out_25, reloj_1_out_28,
       reloj_1_out_29, reloj_1_out_30, reloj_1_out_31, reloj_1_out_33, reloj_1_out_34, reloj_1_out_35,
       reloj_1_out_38, reloj_1_out_39, reloj_1_out_41, reloj_1_out_42, reloj_1_out_43, reloj_1_out_44,
       reloj_1_out_45;

  Mux4Displays7Seg mux4displays7seg_1 (
    .in_1(in_3), .in_2(reloj_1_out_33), .in_3(alarma_1_out_21), .in_4(reloj_1_out_24),
    .in_5(alarma_1_out_15), .in_6(reloj_1_out_9), .in_7(alarma_1_out_4), .in_8(reloj_1_out_5),
    .in_9(alarma_1_out_3), .in_10(reloj_1_out_10), .in_11(alarma_1_out_5), .in_12(reloj_1_out_25),
    .in_13(alarma_1_out_16), .in_14(reloj_1_out_38), .in_15(alarma_1_out_24), .in_16(reloj_1_out_39),
    .in_17(alarma_1_out_25), .in_18(reloj_1_out_28), .in_19(alarma_1_out_17), .in_20(reloj_1_out_14),
    .in_21(alarma_1_out_7), .in_22(reloj_1_out_11), .in_23(alarma_1_out_6), .in_24(reloj_1_out_15),
    .in_25(alarma_1_out_8), .in_26(reloj_1_out_29), .in_27(alarma_1_out_18), .in_28(reloj_1_out_41),
    .in_29(alarma_1_out_26), .in_30(reloj_1_out_42), .in_31(alarma_1_out_27), .in_32(reloj_1_out_30),
    .in_33(alarma_1_out_19), .in_34(reloj_1_out_17), .in_35(alarma_1_out_10), .in_36(reloj_1_out_16),
    .in_37(alarma_1_out_9), .in_38(reloj_1_out_18), .in_39(alarma_1_out_11), .in_40(reloj_1_out_31),
    .in_41(alarma_1_out_20), .in_42(reloj_1_out_43), .in_43(alarma_1_out_28), .in_45(alarma_1_out_29),
    .in_46(reloj_1_out_34), .in_47(alarma_1_out_22), .in_48(reloj_1_out_20), .in_49(alarma_1_out_13),
    .in_50(reloj_1_out_19), .in_51(alarma_1_out_12), .in_52(reloj_1_out_21), .in_53(alarma_1_out_14),
    .in_54(reloj_1_out_35), .in_55(alarma_1_out_23), .in_56(reloj_1_out_45), .in_57(alarma_1_out_30),
    .out_58(out_21), .out_59(out_22), .out_60(out_23), .out_61(out_24), .out_62(out_25), .out_63(out_26),
    .out_64(out_27), .out_65(out_7), .out_66(out_8), .out_67(out_9), .out_68(out_10), .out_69(out_11),
    .out_70(out_12), .out_71(out_13), .out_72(out_14), .out_73(out_15), .out_74(out_16), .out_75(out_17),
    .out_76(out_18), .out_77(out_19), .out_78(out_20), .out_79(out_28), .out_80(out_29), .out_81(out_30),
    .out_82(out_31), .out_83(out_32), .out_84(out_33), .out_85(out_34), .in_44(reloj_1_out_44));
  reloj reloj_1 (
    ._2_3_3(reloj_1__2_3_3), ._2_3_4(reloj_1__2_3_4), ._2_2_3(reloj_1__2_2_3), ._2_3_5(reloj_1__2_3_5),
    ._2_3_6(reloj_1__2_3_6), ._2_2_4(reloj_1__2_2_4), ._2_1_3(reloj_1__2_1_3), ._2_2_5(reloj_1__2_2_5),
    ._2_1_4(reloj_1__2_1_4), ._2_2_6(reloj_1__2_2_6), ._2_0_3(reloj_1__2_0_3), ._2_1_5(reloj_1__2_1_5),
    ._2_0_4(reloj_1__2_0_4), ._2_1_6(reloj_1__2_1_6), ._2_0_5(reloj_1__2_0_5), ._2_0_6(reloj_1__2_0_6),
    .out_33(reloj_1_out_33), .out_24(reloj_1_out_24), .out_9(reloj_1_out_9), .out_5(reloj_1_out_5),
    .out_10(reloj_1_out_10), .out_25(reloj_1_out_25), .out_38(reloj_1_out_38), .out_39(reloj_1_out_39),
    .out_28(reloj_1_out_28), .out_14(reloj_1_out_14), .out_11(reloj_1_out_11), .out_15(reloj_1_out_15),
    .out_29(reloj_1_out_29), .out_41(reloj_1_out_41), .out_42(reloj_1_out_42), .out_30(reloj_1_out_30),
    .out_17(reloj_1_out_17), .out_16(reloj_1_out_16), .out_18(reloj_1_out_18), .out_31(reloj_1_out_31),
    .out_43(reloj_1_out_43), .out_44(reloj_1_out_44), .out_34(reloj_1_out_34), .out_20(reloj_1_out_20),
    .out_19(reloj_1_out_19), .out_21(reloj_1_out_21), .out_35(reloj_1_out_35), .out_45(reloj_1_out_45),
    .out_32(out_35), .out_22(out_36), .out_6(out_37), .out_4(out_38), .out_7(out_39), .out_23(out_40),
    .out_36(out_41), .out_37(out_42), .out_26(out_43), .out_12(out_44), .out_8(out_45), .out_13(out_46),
    .out_27(out_47), .in_3(in_4), .in_2(in_5), .in_1(in_6), .out_40(out_48), ._2_3_2(c4), ._2_2_2(c3),
    ._2_1_2(c2), ._2_0_2(c1), ._2_3(c8), ._2_2(c7), ._2_1(c6), ._2_0(c5));
  alarma alarma_1 (
    ._2_3(alarma_1__2_3), ._2_3_2(alarma_1__2_3_2), ._2_2(alarma_1__2_2), ._2_3_3(alarma_1__2_3_3),
    ._2_3_4(alarma_1__2_3_4), ._2_2_2(alarma_1__2_2_2), ._2_1(alarma_1__2_1), ._2_2_3(alarma_1__2_2_3),
    ._2_1_2(alarma_1__2_1_2), ._2_2_4(alarma_1__2_2_4), ._2_0(alarma_1__2_0), ._2_1_3(alarma_1__2_1_3),
    ._2_0_2(alarma_1__2_0_2), ._2_1_4(alarma_1__2_1_4), ._2_0_3(alarma_1__2_0_3), ._2_0_4(alarma_1__2_0_4),
    .out_21(alarma_1_out_21), .out_15(alarma_1_out_15), .out_4(alarma_1_out_4), .out_3(alarma_1_out_3),
    .out_5(alarma_1_out_5), .out_16(alarma_1_out_16), .out_24(alarma_1_out_24), .out_25(alarma_1_out_25),
    .out_17(alarma_1_out_17), .out_7(alarma_1_out_7), .out_6(alarma_1_out_6), .out_8(alarma_1_out_8),
    .out_18(alarma_1_out_18), .out_26(alarma_1_out_26), .out_27(alarma_1_out_27), .out_19(alarma_1_out_19),
    .out_10(alarma_1_out_10), .out_9(alarma_1_out_9), .out_11(alarma_1_out_11), .out_20(alarma_1_out_20),
    .out_28(alarma_1_out_28), .out_29(alarma_1_out_29), .out_22(alarma_1_out_22), .out_13(alarma_1_out_13),
    .out_12(alarma_1_out_12), .out_14(alarma_1_out_14), .out_23(alarma_1_out_23), .in_2(in_1), .in_1(in_2),
    .out_30(alarma_1_out_30));
  Comparador comparador_1 (
    .A(alarma_1__2_3_4), .a_2(reloj_1__2_3_6), .B(alarma_1__2_2_4), .b_2(reloj_1__2_2_6),
    .C(alarma_1__2_1_4), .c_2(reloj_1__2_1_6), .D(alarma_1__2_0_4), .d_2(reloj_1__2_0_6), .E(alarma_1__2_3),
    .e_2(reloj_1__2_3_3), .F(alarma_1__2_2), .f_2(reloj_1__2_2_3), .G(alarma_1__2_1), .g_2(reloj_1__2_1_3),
    .H(alarma_1__2_0), .h_2(reloj_1__2_0_3), .I(alarma_1__2_3_2), .i_2(reloj_1__2_3_4), .J(alarma_1__2_2_2),
    .j_2(reloj_1__2_2_4), .K(alarma_1__2_1_2), .k_2(reloj_1__2_1_4), .L(alarma_1__2_0_2),
    .l_2(reloj_1__2_0_4), .M(alarma_1__2_3_3), .m_2(reloj_1__2_3_5), .N(alarma_1__2_2_3),
    .n_2(reloj_1__2_2_5), .O(alarma_1__2_1_3), .o_2(reloj_1__2_1_5), .P(alarma_1__2_0_3),
    .p_2(reloj_1__2_0_5), .out_33(out_49));
  LED led_1 (.in(n20seg_1_out_11));
  _20Seg u_20seg_1 (
    .in_1(in_6), .in_2(out_49), .in_3(c8), .in_4(c7), .in_5(c6), .in_6(c5), .in_7(c4), .in_8(c3), .in_9(c2),
    .in_10(c1), .out_11(n20seg_1_out_11));

  // Other names for the same wires on the sheet: Reloj = in_6
endmodule

module switch (
  input  in_1,
  output out_2,
  output out_3
);

  wire d_ff_1_qn, d_ff_2_q, d_ff_2_qn;

  D_Flip_Flop d_ff_1 (.clk(in_1), .D(d_ff_2_qn), .Qn(d_ff_1_qn));  // open: Q, preset, en, reset
  D_Flip_Flop d_ff_2 (.clk(in_1), .D(d_ff_1_qn), .Q(d_ff_2_q), .Qn(d_ff_2_qn));  // open: preset, en, reset
  Demultiplexer demultiplexer_1 (.out0(out_2), .out1(out_3), .in(1'b1), .sel(d_ff_2_q));  // open: en
endmodule

module Botones (
  input  in_1,
  input  in_2,
  input  in_3,
  output out_4,
  output out_5
);

  and and_1 (out_4, in_1, in_2);
  and and_2 (out_5, in_1, in_3);
endmodule

module Reloj20Seg (
  input  in_1,
  output out_2,
  output out_3,
  output out_4,
  output out_5,
  output out_6,
  output out_7,
  output out_8,
  output out_9,
  output out_10,
  output out_11,
  output out_12,
  output out_13,
  output out_14,
  output out_15,
  output _2_3,
  output _2_3_2,
  output _2_2,
  output _2_2_2,
  output _2_1,
  output _2_1_2,
  output _2_0,
  output _2_0_2
);

  wire and_1_out, and_2_out;

  DecoLED decoled_1 (
    .I4(_2_3), .I3(_2_2), .I2(_2_1), .I1(_2_0), .o1(out_12), .o2(out_8), .o3(out_3), .o5(out_2), .o6(out_4),
    .o7(out_9), .o8(out_13));
  and and_1 (and_1_out, _2_0_2, _2_1);
  cont4Bit cont4bit_1 (.T(and_2_out), .Reset(and_1_out), .Q3(_2_3), .Q2(_2_2), .Q1(_2_1), .Q0(_2_0));
  and and_2 (and_2_out, _2_3_2, _2_1_2);
  DecoLED decoled_2 (
    .I4(_2_3_2), .I3(_2_2_2), .I2(_2_1_2), .I1(_2_0_2), .o1(out_14), .o2(out_10), .o3(out_6), .o5(out_5),
    .o6(out_7), .o7(out_11), .o8(out_15));
  cont4Bit cont4bit_2 (.T(in_1), .Reset(and_2_out), .Q3(_2_3_2), .Q2(_2_2_2), .Q1(_2_1_2), .Q0(_2_0_2));
endmodule

module Comparador20Seg (
  input  A,
  input  a_2,
  input  B,
  input  b_2,
  input  C,
  input  c_2,
  input  D,
  input  d_2,
  input  E,
  input  e_2,
  input  F,
  input  f_2,
  input  G,
  input  g_2,
  input  H,
  input  h_2,
  output out_17
);

  wire comparator_1_eq, comparator_2_eq, comparator_3_eq, comparator_4_eq, comparator_5_eq, comparator_6_eq,
       comparator_7_eq, comparator_8_eq;

  Comparator #(.width(1)) comparator_1 (.a(A), .b(a_2), .eq(comparator_1_eq));  // open: gt, lt
  Comparator #(.width(1)) comparator_2 (.a(B), .b(b_2), .eq(comparator_2_eq));  // open: gt, lt
  Comparator #(.width(1)) comparator_3 (.a(C), .b(c_2), .eq(comparator_3_eq));  // open: gt, lt
  Comparator #(.width(1)) comparator_4 (.a(D), .b(d_2), .eq(comparator_4_eq));  // open: gt, lt
  Comparator #(.width(1)) comparator_5 (.a(E), .b(e_2), .eq(comparator_5_eq));  // open: gt, lt
  Comparator #(.width(1)) comparator_6 (.a(F), .b(f_2), .eq(comparator_6_eq));  // open: gt, lt
  Comparator #(.width(1)) comparator_7 (.a(G), .b(g_2), .eq(comparator_7_eq));  // open: gt, lt
  Comparator #(.width(1)) comparator_8 (.a(H), .b(h_2), .eq(comparator_8_eq));  // open: gt, lt
  and and_1 (out_17, comparator_1_eq, comparator_2_eq, comparator_3_eq, comparator_4_eq, comparator_5_eq, comparator_6_eq, comparator_7_eq, comparator_8_eq);

  // Notes on the sheet:
  //   20 Seg completados
endmodule

module _20Seg (
  input  in_1,
  input  in_2,
  input  in_3,
  input  in_4,
  input  in_5,
  input  in_6,
  input  in_7,
  input  in_8,
  input  in_9,
  input  in_10,
  output out_11
);

  wire and_1_out, and_2_out, and_3_out, and_4_out, and_5_out, and_6_out, and_7_out, and_8_out, and_9_out, r1,
       r2, r3, r4, r5, r6, r7, r8, r9, r10, r11, r12, r13, r14, reloj20seg_1__2_0, reloj20seg_1__2_0_2,
       reloj20seg_1__2_1, reloj20seg_1__2_1_2, reloj20seg_1__2_2, reloj20seg_1__2_2_2, reloj20seg_1__2_3,
       reloj20seg_1__2_3_2;

  and and_1 (and_1_out, in_1, in_2);
  _7_Segment_Display u_7_segment_display_1 (.g(r11), .f(r12), .a(r13), .b(r14), .e(r8), .d(r9), .c(r10));  // open: dp
  _7_Segment_Display u_7_segment_display_2 (.g(r4), .f(r5), .a(r6), .b(r7), .e(r1), .d(r2), .c(r3));  // open: dp
  Reloj20Seg reloj20seg_1 (
    .in_1(and_1_out), ._2_3(reloj20seg_1__2_3), ._2_3_2(reloj20seg_1__2_3_2), ._2_2(reloj20seg_1__2_2),
    ._2_2_2(reloj20seg_1__2_2_2), ._2_1(reloj20seg_1__2_1), ._2_1_2(reloj20seg_1__2_1_2),
    ._2_0(reloj20seg_1__2_0), ._2_0_2(reloj20seg_1__2_0_2), .out_12(r8), .out_8(r9), .out_3(r10),
    .out_2(r11), .out_4(r12), .out_9(r13), .out_13(r14), .out_14(r1), .out_10(r2), .out_6(r3), .out_5(r4),
    .out_7(r5), .out_11(r6), .out_15(r7));
  and and_2 (and_2_out, and_1_out, in_3);
  and and_3 (and_3_out, and_1_out, in_4);
  and and_4 (and_4_out, and_1_out, in_5);
  and and_5 (and_5_out, and_1_out, in_6);
  and and_6 (and_6_out, and_1_out, in_7);
  and and_7 (and_7_out, and_1_out, in_8);
  and and_8 (and_8_out, and_1_out, in_9);
  and and_9 (and_9_out, and_1_out, in_10);
  LED _20_Seg_Completos (.in(out_11));
  Comparador20Seg comparador20seg_1 (
    .A(reloj20seg_1__2_3), .a_2(and_2_out), .B(reloj20seg_1__2_2), .b_2(and_3_out), .C(reloj20seg_1__2_1),
    .c_2(and_4_out), .D(reloj20seg_1__2_0), .d_2(and_5_out), .E(reloj20seg_1__2_3_2), .e_2(and_6_out),
    .F(reloj20seg_1__2_2_2), .f_2(and_7_out), .G(reloj20seg_1__2_1_2), .g_2(and_8_out),
    .H(reloj20seg_1__2_0_2), .h_2(and_9_out), .out_17(out_11));
endmodule
